// Logisim project real alu.circ as structural Verilog
module a_AND_b (
  input  [7:0] in_1,
  input  [7:0] in_2,
  output [7:0] out_3
);

  assign out_3 = in_1 & in_2;  // AND_Gate and_1, 8 bits wide
endmodule

module a_OR_b (
  input  [7:0] in_1,
  input  [7:0] in_2,
  output [7:0] out_3
);

  assign out_3 = in_1 | in_2;  // OR_Gate or_1, 8 bits wide
endmodule

module NOT_b (
  input  [7:0] in_1,
  output [7:0] out_2
);

  assign out_2 = in_1;  // Buffer buffer_1, 8 bits wide
endmodule
